// Logisim project task2_mealy.circ as structural Verilog: 7 circuits, main circuit main
module main (
  output INPUT,
  output OUTPUT
);

  wire clock_1_out, Inputs_a, Inputs_b, Outputs_alpha, Outputs_beta, States_delay, States_first,
       States_second, States_start, States_success, States_successd, undriven, undriven_2;
  wire [2:0] nextstatelogic_1_ns, register_1_q;

  Clock clock_1 (.out(clock_1_out));
  LED a0 (.in(Inputs_a));
  LED b1 (.in(Inputs_b));
  InputVisualisation Inputs (.I(INPUT), .a(Inputs_a), .b(Inputs_b));
  TestSequence testsequence_1 (.CLK(clock_1_out), .I_test(INPUT));
  LED FIRST (.in(States_first));
  LED START (.in(States_start));
  NextStateLogic nextstatelogic_1 (.I(INPUT), .S(register_1_q), .NS(nextstatelogic_1_ns));
  LED DELAY (.in(States_delay));
  LED SECOND (.in(States_second));
  StateVisualisation States (
    .in_1(register_1_q), .START(States_start), .FIRST(States_first), .SECOND(States_second),
    .DELAY(States_delay), .SUCCESSD(States_successd), .SUCCESS(States_success));
  Register #(.width(3)) register_1 (
    .D(nextstatelogic_1_ns), .en(undriven), .clk(clock_1_out), .Q(register_1_q), .clr(undriven_2));
  // NoConnect on undriven
  // NoConnect on undriven_2
  LED SUCCESS (.in(States_success));
  LED SUCCESSD (.in(States_successd));
  LED alpha0 (.in(Outputs_alpha));
  OutputVisualisation Outputs (.O(OUTPUT), .alpha(Outputs_alpha), .beta(Outputs_beta));
  OutputLogic outputlogic_1 (.I(INPUT), .S(register_1_q), .O(OUTPUT));
  LED beta1 (.in(Outputs_beta));

  // Notes on the sheet:
  //   TASK 2 - MEALY MACHINE
endmodule

module NextStateLogic (
  input  I,
  input  [2:0] S,
  output [2:0] NS
);

  ROM #(.addrWidth(4), .dataWidth(3)) rom_1 (.addr({S, I}), .data(NS));

  // Notes on the sheet:
  //   contents of rom_1 (hex, n*v repeats v):
  //   1 0 1 2 3 5 3 4 3 5 1 0 4*3
endmodule

module OutputLogic (
  input  I,
  input  [2:0] S,
  output O
);

  ROM #(.addrWidth(4), .dataWidth(1)) rom_1 (.addr({S, I}));  // open: data

  // Notes on the sheet:
  //   contents of rom_1 (hex, n*v repeats v):
  //   5*0 1 0 1 0 1 0 0 4*1
endmodule

module InputVisualisation (
  input  I,
  output a,
  output b
);

  and and_1 (a, ~I, ~I);  // AND_Gate
  and and_2 (b, I, I);
endmodule

module StateVisualisation (
  input  [2:0] in_1,
  output START,
  output FIRST,
  output SECOND,
  output DELAY,
  output SUCCESSD,
  output SUCCESS
);

  and and_1 (START, ~in_1[2], ~in_1[1], ~in_1[0]);  // AND_Gate
  and and_2 (FIRST, ~in_1[2], ~in_1[1], in_1[0]);  // AND_Gate
  and and_3 (SECOND, ~in_1[2], in_1[1], ~in_1[0]);  // AND_Gate
  and and_4 (DELAY, ~in_1[2], in_1[1], in_1[0]);  // AND_Gate
  and and_5 (SUCCESSD, in_1[2], ~in_1[1], ~in_1[0]);  // AND_Gate
  and and_6 (SUCCESS, in_1[2], ~in_1[1], in_1[0]);  // AND_Gate
endmodule

module OutputVisualisation (
  input  O,
  output alpha,
  output beta
);

  and and_1 (alpha, ~O, ~O);  // AND_Gate
  and and_2 (beta, O, O);
endmodule

module TestSequence (
  input  CLK,
  output I_test
);

  wire [3:0] counter_1_q;

  ROM #(.addrWidth(4), .dataWidth(1)) rom_1 (.addr(counter_1_q));  // open: data
  Counter #(.max('hf), .width(4)) counter_1 (.Q(counter_1_q), .clk(CLK));  // open: load, D, count, carry, up, clr

  // Notes on the sheet:
  //   contents of rom_1 (hex, n*v repeats v):
  //   1 0 0 1 1 0 1 0 0 1 0 5*1
endmodule
